// Logisim project jws146_lab6.circ as structural Verilog: 1 circuit, main circuit main
module main (
);

  wire button_1_out, CLK, CMD_T_out;

  Clock CMD_T (.out(CMD_T_out));
  Button button_1 (.out(button_1_out));
  or or_1 (CLK, CMD_T_out, button_1_out);

  // Notes on the sheet:
  //   connect clock signal to registers
endmodule
